# Fritzing sketch Dust Sketch (saved by Fritzing 0.9.3b)
perfboards: 2
stripboards: 1

parts:
  U1 = RELAY-SOLIDSTATE [package=relay-s108t02]
  J2 = T Cobbler Plus
  J6 = Screw terminal - 2 pins [package=THT]
  J8 = male pin header, 4 pins [form="♂ (male)"]
  U6 = Voltage Regulator [package=to220-adj]
  R4 = Resistor [tolerance=±5% resistance=220 package="1206 [SMD]"]
  R5 = Resistor [tolerance=±5% resistance=220 package="1206 [SMD]"]
  R6 = Resistor [tolerance=±5% resistance=220 package="1206 [SMD]"]
  U7 = OP27 - Low Noise, Precision Op Amp [part_number=OP27]
  J7 = screw terminal, 2 pins
  J9 = female pin header, 2 pins [form="♀ (female)"]
  J10 = female pin header, 4 pins [form="♀ (female)"]
  J11 = female pin header, 4 pins [form="♀ (female)"]
  J12 = female pin header, 4 pins [form="♀ (female)"]
  S1 = Toggle Switch [package=THT]
  U8 = Molex Picoblade Series Header [part_number=0532610219 package=Picoblade-53261-0219]
  U9 = Hirose DF13 Series Header [part_number=DF13#-3P-1.25V package=DF13C-3P-1.25V]
  J13 = female pin header, 20 pins [form="♀ (female)"]
  J14 = female pin header, 20 pins [form="♀ (female)"]
  Mod1 = Raspberry Pi 4B
  Part3 = Adafruit TFP401 to 40 pin TFT with Touch [part_number="Adafruit #2219"]  # not connected
  J15 = female pin header, 4 pins [form="♀ (female)"]
  J16 = female pin header, 4 pins [form="♀ (female)"]
  HLK-PM1 = HLK-PM01

nets:
  N1: U1.T1, J7.pin2, S1.L2, HLK-PM1.AC#1
  N2: U1.T2, U8.2
  N3: U1.+, J9.pin2, J14.pin8
  N4: U1.-, J9.pin1
  3.3V: J2.3.3V, Mod1.3V3
  5V: J2.5V, Mod1.5V
  N5: J2.GPIO_2, Mod1.GPIO2
  N6: J2.GPIO_3, Mod1.GPIO3
  GND: J2.GND, Mod1.GND
  N7: J2.GPIO_4, Mod1.GPIO4
  N8: J2.GPIO_14, Mod1.GPIO14
  N9: J2.GPIO_15, Mod1.GPIO15
  N10: J2.GPIO_17, Mod1.GPIO17
  N11: J2.GPIO_18, Mod1.GPIO18
  N12: J2.GPIO_27, Mod1.GPIO27
  N13: J2.GPIO_22, Mod1.GPIO22
  N14: J2.GPIO_23, Mod1.GPIO23
  N15: J2.GPIO_24, Mod1.GPIO24
  N16: J2.GPIO_10, Mod1.GPIO10
  N17: J2.GPIO_9, Mod1.GPIO9
  N18: J2.GPIO_25, Mod1.GPIO25
  N19: J2.GPIO_11, Mod1.GPIO11
  N20: J2.GPIO_8, Mod1.GPIO8
  N21: J2.GPIO_7, Mod1.GPIO7
  N22: J2.ID_SD, Mod1.ID_SD
  N23: J2.ID_SC, Mod1.ID_SC
  N24: J2.GPIO_5, Mod1.GPIO5
  N25: J2.GPIO_6, Mod1.GPIO6
  N26: J2.GPIO_12, Mod1.GPIO12
  N27: J2.GPIO_13, Mod1.GPIO13
  N28: J2.GPIO_19, Mod1.GPIO19
  N29: J2.GPIO_16, Mod1.GPIO16
  N30: J2.GPIO_26, Mod1.GPIO26
  N31: J2.GPIO_20, Mod1.GPIO20
  N32: J2.GPIO_21, Mod1.GPIO21
  N33: J6.pin2, U9.2
  N34: J8.pin4, J10.pin2
  N35: U6.ADJ, R6.Pin_0
  N36: U6.IN, R4.Pin_0, U7.OUT
  N37: U6.OUT, R5.Pin_0
  N38: J7.pin1, S1.COM, U8.1, HLK-PM1.AC#0
  N39: J11.pin3, J15.pin3
  N40: J11.pin4, J15.pin4
  N41: J12.pin3, J16.pin3
  N42: J12.pin4, J16.pin4
  N43: S1.L1, U9.1
  N44: J13.pin14, J16.pin2
  N45: J14.pin4, J15.pin2
  N46: J14.pin5, J15.pin1
  N47: J14.pin14, J16.pin1

notes:
  LOAD
  AC-IN
  VCC GND Z-C PWM
  AC plug
  ESP
  FAN
  HDMI to micro HDMI
  Display
  USB to micro USB
  Raspberry Pi 4
  Main Board
  AC Light Dimmer
  Solid State Relay
  PMS7003_1
  PMS7003_2
  Adapter
  TX RX VCC GND
  GND Out
  RX TX VCC GND
  USB Type C

custom parts:
  T Cobbler Plus: The T-Cobbler Plus is an add on prototyping board from Adafruit specifically designed for the Raspberry Pi B+ that can break out all those tasty power, GPIO, I2C and SPI pins from the 40-pin header onto a solderless breadboard. This set will make "cobbling together" prototypes with the Pi super easy. The T-Cobbler Plus can plug into any solderless breadboard.
  Adafruit TFP401 to 40 pin TFT with Touch: It's a mini HDMI decoder board! So small and simple, you can use this board as an all-in-one display driver for TTL displays, or perhaps decoding HDMI/DVI video for some other project. This breakout features the TFP401 for decoding video, and for the touch version, an AR1100 USB resistive touch screen driver. The TFP401 is a beefy DVI/HDMI decoder from TI. It can take unencrypted video and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
